# Fritzing sketch coderdojo-trafficlights (saved by Fritzing 1.0.4)
breadboards: 1

parts:
  A1 = Calliope mini 3
  LED1 = LED - 5mm [color="Red (633nm)" current=0.030A package="5 mm [THT]"]
  LED2 = LED - 5mm [color="Green (555nm)" current=0.030A package="5 mm [THT]"]
  LED3 = LED - 5mm [color="Yellow (585nm)" current=0.030A package="5 mm [THT]"]
  S1 = Pushbutton [package="[THT]"]

nets:
  N1: A1.Pin_9, LED2.anode
  N2: A1.Pin_10, S1.Pin_1, S1.Pin_2
  N3: A1.Pin_19, A1.Pin_23, A1.Pin_46, LED1.cathode, LED2.cathode, LED3.cathode, S1.Pin_3, S1.Pin_4
  N4: A1.Pin_24, LED1.anode
  N5: A1.Pin_25, A1.Pin_44, LED3.anode

notes:
  Schaltplan für Anbindung LED und Schalter
  an Calliope Mini v3 für Ampelschaltung
  Code: https://github.com/egoexpress/coderdojo-trafficlights
  Version vom 2025-01-26
